# Fritzing sketch Tejas-Avionics-PCB (saved by Fritzing 0.9.3b)
circuit board: 10cm x 6cm
perfboards: 1

parts:
  Part1 = Arduino Nano (Rev3.0)
  Part2 = InvenSense MPU6050
  Part3 = GY-BMEP280 Barometric Pressure Sensor - Breakout
  D1 = LTE-302 [package=lte-302]  # not connected
  microSD1 = MicroSD Card Module

nets:
  GND: Part1.GND, Part2.GND, Part3.GND, microSD1.GND
  N1: Part1.D4, microSD1.CS
  VCC: Part1.5V, Part2.VCC, microSD1.VCC
  N2: Part1.A5, Part2.SCL
  N3: Part1.A4, Part2.SDA
  3V3: Part1.3V3, Part3.VCC

notes:
  RED - TOP
  BLUE - BELLOW

custom parts:
  GY-BMEP280 Barometric Pressure Sensor - Breakout: The BME280 is a chip which was originally designed for the next generation of smartphones. It is made up of a very accurate pressure sensor and an associated temperature sensor which helps calibrate the pressure readings. And just for fun they threw in a pretty solid humidity sensor in there as well! So with an I2C connection you have access to enough weather data to make some pretty good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
